# Fritzing sketch arduino_linear_pot (saved by Fritzing 0.9.3b)

parts:
  R1 = Slide Potentiometer [maximum_resistance=100kΩ]
  Part1 = Arduino Uno (Rev3)

nets:
  N1: R1.leg1, Part1.GND
  N2: R1.wiper, Part1.A0
  N3: R1.leg2, Part1.5V

notes:
  Pin 1
  Pin 2
  Pin 3
